# Fritzing sketch Liquid Crystal + HC-SR04+Buzzer (saved by Fritzing 0.9.1b)
breadboards: 1

parts:
  Onderdeel1 = Arduino Uno (Rev3)
  LCD1 = LCD screen
  R1 = Rotary Potentiometer (Small) [maximum_resistance=100kΩ package=THT]  # not connected
  Onderdeel2 = SRF05 Ultrasonic Rangefinder  # not connected
  J1 = Piezo Speaker  # not connected

nets:
  N1: Onderdeel1.D11_PWM/MOSI, LCD1.E
  N2: Onderdeel1.D12/MISO, LCD1.RS
  GND: Onderdeel1.GND, LCD1.VSS, LCD1.R/W, LCD1.LED-
  N3: Onderdeel1.D2, LCD1.DB7
  N4: Onderdeel1.D3_PWM, LCD1.DB6
  N5: Onderdeel1.D4, LCD1.DB5
  N6: Onderdeel1.D5_PWM, LCD1.DB4
  N7: Onderdeel1.3V3, LCD1.LED+
  5V: Onderdeel1.5V, LCD1.VDD
