# Fritzing sketch Liquid Crystal + NTC + LCD (saved by Fritzing 0.9.1b)
breadboards: 1

parts:
  Onderdeel1 = Arduino Uno (Rev3)
  LCD1 = LCD screen
  R1 = Rotary Potentiometer (Small) [maximum_resistance=100kΩ package=THT]  # not connected
  R5 = Temperature Sensor (Thermistor) [thermistor_type=NTC package=THT]
  R6 = 10k Ω Resistor [package=THT]

nets:
  N1: Onderdeel1.A0, R5.pin_1, R6.Pin_0
  N2: Onderdeel1.D11_PWM/MOSI, LCD1.E
  N3: Onderdeel1.D12/MISO, LCD1.RS
  N4: Onderdeel1.D2, LCD1.DB7
  N5: Onderdeel1.D3_PWM, LCD1.DB6
  N6: Onderdeel1.D4, LCD1.DB5
  N7: Onderdeel1.D5_PWM, LCD1.DB4
  N8: Onderdeel1.3V3, LCD1.LED+
  5V: Onderdeel1.5V, LCD1.VDD, R5.pin_0
  GND: Onderdeel1.GND, LCD1.VSS, LCD1.R/W, LCD1.LED-, R6.Pin_1

notes:
  NTC (Thermistor)

custom parts:
  10k Ω Resistor: A generic resistor (0.25W)
