# Fritzing sketch Liquid Crystal + Potmeter (saved by Fritzing 0.9.1b)
breadboards: 1

parts:
  Onderdeel1 = Arduino Uno (Rev3)
  R6 = TRIMPOT [package=trimpot_pth_s3_lock]

nets:
  N1: Onderdeel1.A0, R6.WIPER
  N2: Onderdeel1.5V, R6.CW
  N3: Onderdeel1.GND, R6.CCW
