# Fritzing sketch RGB_Autofader (saved by Fritzing 0.9.1b)
breadboards: 1

parts:
  Onderdeel1 = Arduino Uno (Rev3)
  LED1 = RGB LED (com. cathode, rgb) [package="5 mm [THT]"]
  R3 = Resistor [tolerance=±5% resistance=330 package=THT]
  R4 = Resistor [tolerance=±5% resistance=330 package=THT]
  R5 = Resistor [tolerance=±5% resistance=330 package=THT]

nets:
  N1: Onderdeel1.D3_PWM, R5.Pin_1
  N2: Onderdeel1.D5_PWM, R4.Pin_1
  N3: Onderdeel1.D6_PWM, R3.Pin_1
  N4: Onderdeel1.GND, LED1.green_anode
  N5: LED1.red_anode, R3.Pin_0
  N6: LED1.common_cathode, R4.Pin_0
  N7: LED1.blue_anode, R5.Pin_0

notes:
  RGB Common cathode
