# Fritzing sketch TMP36 v2 (saved by Fritzing 0.9.1b)
breadboards: 1

parts:
  Onderdeel1 = Arduino Uno (Rev3)
  T1 = TMP36 Temperature Sensor [package="TO92 [THT]"]

nets:
  N1: Onderdeel1.A0, T1.Vout
  N2: Onderdeel1.AREF, Onderdeel1.3V3, T1.+Vs
  GND: Onderdeel1.GND, T1.GND
