# Fritzing sketch Temperatuur meter DS18B20 (saved by Fritzing 0.9.1b)
breadboards: 1

parts:
  Onderdeel1 = Arduino Uno (Rev3)
  R1 = 4k7 Ω Resistor [package=THT]
  DS4 = DS18B20 1-Wire Temperature Sensor Probe Cable
  DS5 = DS18B20 1-Wire Temperature Sensor Probe Cable
  DS6 = DS18B20 1-Wire Temperature Sensor Probe Cable

nets:
  N1: Onderdeel1.D3_PWM, R1.Pin_0, DS4.DQ, DS5.DQ, DS6.DQ
  VDD: Onderdeel1.5V, R1.Pin_1, DS4.VDD, DS5.VDD, DS6.VDD
  GND: Onderdeel1.GND, DS4.GND, DS5.GND, DS6.GND

notes:
  Er is maar één pull-up weerstand nodig van 4k7 nodig.....

custom parts:
  4k7 Ω Resistor: A generic resistor (0.25W)
