# Fritzing sketch Temperatuur meter IR TMP006 (saved by Fritzing 0.9.1b)
breadboards: 1

parts:
  Onderdeel1 = Arduino Uno (Rev3)
  TMP1 = TMP006 Temperature Sensor
  R1 = 10k Ω Resistor [package=THT]
  R2 = 10k Ω Resistor [package=THT]

nets:
  N1: Onderdeel1.A4/SDA, TMP1.SDA, R1.Pin_0
  N2: Onderdeel1.A5/SCL, TMP1.SCL, R2.Pin_0
  GND: Onderdeel1.GND, TMP1.GND
  N3: TMP1.VCC, R1.Pin_1, R2.Pin_1

custom parts:
  TMP006 Temperature Sensor: TMP006 Contact-less Infrared Thermopile Sensor Breakout
  10k Ω Resistor: A generic resistor (0.25W)
