# Fritzing sketch Vochtigheids meting DHT11 (saved by Fritzing 0.9.1b)
breadboards: 1

parts:
  Onderdeel1 = Arduino Uno (Rev3)
  DHT1 = DHT11 Humitidy and Temperature Sensor

nets:
  N1: Onderdeel1.D2, DHT1.DATA
  5V: Onderdeel1.5V, DHT1.VDD
  GND: Onderdeel1.GND, DHT1.GND

custom parts:
  DHT11 Humitidy and Temperature Sensor: DHT11 Humidity and Temperature Sensor
